# Fritzing sketch CircuitoRobot (saved by Fritzing 0.9.3b)
breadboards: 1

parts:
  Componente1 = Arduino Uno (Rev3) - ICSP
  M2 = DC Motor
  M3 = DC Motor
  S1 = H-Bridge with L298N
  BATT1 = 4xAA Switchable Battery Pack w/Bare Wire
  hc-sr1 = hc-sr04
  J1 = Piezo Speaker

nets:
  N1: Componente1.D8, S1.IN2
  N2: Componente1.D9_PWM, S1.IN1
  N3: Componente1.D10_PWM/SS, S1.ENB
  N4: Componente1.D11_PWM/MOSI, S1.ENA
  N5: Componente1.D12/MISO, S1.IN4
  N6: Componente1.D13/SCK, S1.IN3
  N7: Componente1.D4, hc-sr1.Echo
  N8: Componente1.D5_PWM, hc-sr1.Trig
  N9: Componente1.D6_PWM, J1.pin2
  5V: Componente1.5V, hc-sr1.VCC
  GND: Componente1.GND, S1.GND, BATT1.NEG, hc-sr1.GND, J1.pin1
  N10: M2.pin_1, S1.M1-02
  N11: M2.pin_2, S1.M1-01
  N12: M3.pin_1, S1.M2-01
  N13: M3.pin_2, S1.M2-02
  N14: S1.12V, BATT1.POS

custom parts:
  H-Bridge with L298N: h-bridge
  4xAA Switchable Battery Pack w/Bare Wire: 4xAA Switchable Battery Pack with Bare Wire connection
